// Logisim project Multiplexers.circ as structural Verilog: 2 circuits, main circuit mx2i_1
module mx2i_1 (
  input  in0,
  input  s,
  input  in1,
  output z
);

  wire nand_1_out, nand_2_out, not_1_out;

  not not_1 (not_1_out, s);
  nand nand_1 (nand_1_out, in0, not_1_out);
  nand nand_2 (nand_2_out, s, in1);
  nand nand_3 (z, nand_1_out, nand_2_out);

  // Notes on the sheet:
  //   14 Transistors
  //   2:1 Mux
  //   Malcolmb Roalson
  //   max(s+2.75, in0+2, in1+2)
endmodule

module mx4i_1 (
  input  in0,
  input  in1,
  input  in2,
  input  s1,
  input  in3,
  input  s0,
  output z
);

  wire mx2i_1_1_z, mx2i_1_2_z;

  mx2i_1 mx2i_1_1 (.in0(in0), .s(s0), .in1(in1), .z(mx2i_1_1_z));
  mx2i_1 mx2i_1_2 (.in0(in2), .s(s0), .in1(in3), .z(mx2i_1_2_z));
  mx2i_1 mx2i_1_3 (.in0(mx2i_1_1_z), .s(s1), .in1(mx2i_1_2_z), .z(z));

  // Notes on the sheet:
  //   42 Transistors
  //   4:1 Mux
  //   Malcolmb Roalson
  //   max(s0+4.75, s1+2.75, in0+4, in1+4, in2+4, in3+4)
endmodule
