// Logisim project Multipliers.circ as structural Verilog
module FA (
  input  a,
  input  b,
  input  cin,
  output cout,
  output s
);

  FAopt1 faopt1_1 (.a(a), .b(b), .cin(cin), .s(s), .cout(cout));
endmodule

module uMull8 (
  input  [7:0] A,
  input  [7:0] B,
  output [15:0] AB
);

  wire fa_2_cout, fa_2_s, fa_3_cout, fa_3_s, fa_5_cout, fa_5_s, fa_6_cout, fa_6_s, fa_7_cout, fa_7_s,
       fa_9_cout, fa_9_s, fa_10_cout, fa_10_s, fa_11_cout, fa_11_s, fa_12_cout, fa_12_s, fa_13_cout, fa_13_s,
       fa_14_cout, fa_14_s, fa_16_cout, fa_16_s, fa_17_cout, fa_17_s, fa_18_cout, fa_18_s, fa_20_cout,
       fa_20_s, fa_21_cout, fa_21_s, fa_22_cout, fa_22_s, fa_23_cout, fa_23_s, fa_24_cout, fa_24_s,
       fa_26_cout, fa_26_s, fa_27_cout, fa_27_s, fa_28_cout, fa_28_s, fa_29_cout, fa_29_s, fa_31_cout,
       fa_31_s, fa_32_cout, fa_32_s, fa_33_cout, fa_33_s, fa_34_cout, fa_34_s, fa_36_cout, fa_36_s,
       fa_37_cout, fa_37_s, fa_38_cout, fa_38_s, fa_39_cout, fa_39_s, fa_40_cout, fa_40_s, fa_42_cout,
       fa_42_s, fa_43_cout, fa_43_s, fa_44_cout, fa_44_s, fa_45_cout, fa_45_s, fa_47_cout, fa_47_s,
       fa_48_cout, fa_48_s, fa_49_cout, fa_49_s, fa_51_cout, fa_51_s, fa_52_cout, fa_52_s, fa_53_cout,
       fa_54_cout, fa_54_s, fa_55_cout, fa_56_cout;
  wire [7:0] r0, r1, r2, r3, r4, r5, r6, r7;
  wire [15:0] undriven;
  wire [15:1] fa_56_s;

  and and_1 (r0[7], B[0], A[7]);
  and and_2 (r1[7], B[1], A[7]);
  and and_3 (r2[7], B[2], A[7]);
  and and_4 (r3[7], B[3], A[7]);
  and and_5 (r4[7], B[4], A[7]);
  and and_6 (r5[7], B[5], A[7]);
  and and_7 (r6[7], B[6], A[7]);
  and and_8 (r7[7], B[7], A[7]);
  and and_9 (r0[6], B[0], A[6]);
  and and_10 (r1[6], B[1], A[6]);
  and and_11 (r2[6], B[2], A[6]);
  and and_12 (r3[6], B[3], A[6]);
  and and_13 (r4[6], B[4], A[6]);
  and and_14 (r5[6], B[5], A[6]);
  and and_15 (r6[6], B[6], A[6]);
  and and_16 (r7[6], B[7], A[6]);
  and and_17 (r0[5], B[0], A[5]);
  and and_18 (r1[5], B[1], A[5]);
  and and_19 (r2[5], B[2], A[5]);
  and and_20 (r3[5], B[3], A[5]);
  and and_21 (r4[5], B[4], A[5]);
  and and_22 (r5[5], B[5], A[5]);
  and and_23 (r6[5], B[6], A[5]);
  and and_24 (r7[5], B[7], A[5]);
  and and_25 (r0[4], B[0], A[4]);
  and and_26 (r1[4], B[1], A[4]);
  and and_27 (r2[4], B[2], A[4]);
  and and_28 (r3[4], B[3], A[4]);
  and and_29 (r4[4], B[4], A[4]);
  and and_30 (r5[4], B[5], A[4]);
  and and_31 (r6[4], B[6], A[4]);
  and and_32 (r7[4], B[7], A[4]);
  and and_33 (r0[3], B[0], A[3]);
  and and_34 (r1[3], B[1], A[3]);
  and and_35 (r2[3], B[2], A[3]);
  and and_36 (r3[3], B[3], A[3]);
  and and_37 (r4[3], B[4], A[3]);
  and and_38 (r5[3], B[5], A[3]);
  and and_39 (r6[3], B[6], A[3]);
  and and_40 (r7[3], B[7], A[3]);
  and and_41 (r0[2], B[0], A[2]);
  and and_42 (r1[2], B[1], A[2]);
  and and_43 (r2[2], B[2], A[2]);
  and and_44 (r3[2], B[3], A[2]);
  and and_45 (r4[2], B[4], A[2]);
  and and_46 (r5[2], B[5], A[2]);
  and and_47 (r6[2], B[6], A[2]);
  and and_48 (r7[2], B[7], A[2]);
  and and_49 (r0[1], B[0], A[1]);
  and and_50 (r1[1], B[1], A[1]);
  and and_51 (r2[1], B[2], A[1]);
  and and_52 (r3[1], B[3], A[1]);
  and and_53 (r4[1], B[4], A[1]);
  and and_54 (r5[1], B[5], A[1]);
  and and_55 (r6[1], B[6], A[1]);
  and and_56 (r7[1], B[7], A[1]);
  and and_57 (r0[0], B[0], A[0]);
  and and_58 (r1[0], B[1], A[0]);
  and and_59 (r2[0], B[2], A[0]);
  and and_60 (r3[0], B[3], A[0]);
  and and_61 (r4[0], B[4], A[0]);
  and and_62 (r5[0], B[5], A[0]);
  and and_63 (r6[0], B[6], A[0]);
  and and_64 (r7[0], B[7], A[0]);
  FA fa_1 (.a(fa_3_cout), .b(fa_2_cout), .cin(r7[7]), .s(undriven[14]), .cout(fa_56_s[15]));
  FA fa_2 (.a(fa_5_cout), .b(r7[6]), .cin(r6[7]), .s(fa_2_s), .cout(fa_2_cout));
  FA fa_3 (.a(fa_6_cout), .b(fa_2_s), .s(fa_3_s), .cout(fa_3_cout));  // open: cin
  FA fa_4 (.a(fa_7_cout), .b(fa_3_s), .s(undriven[13]), .cout(fa_56_s[14]));  // open: cin
  FA fa_5 (.a(r7[5]), .b(r6[6]), .cin(r5[7]), .s(fa_5_s), .cout(fa_5_cout));
  FA fa_6 (.a(fa_9_cout), .b(fa_5_s), .s(fa_6_s), .cout(fa_6_cout));  // open: cin
  FA fa_7 (.a(fa_10_cout), .b(fa_6_s), .s(fa_7_s), .cout(fa_7_cout));  // open: cin
  FA fa_8 (.a(fa_14_cout), .b(fa_7_s), .s(undriven[12]), .cout(fa_56_s[13]));  // open: cin
  FA fa_9 (.a(r6[5]), .b(r5[6]), .cin(r4[7]), .s(fa_9_s), .cout(fa_9_cout));
  FA fa_10 (.a(fa_11_cout), .b(r7[4]), .cin(fa_9_s), .s(fa_10_s), .cout(fa_10_cout));
  FA fa_11 (.a(r4[6]), .b(r3[7]), .s(fa_11_s), .cout(fa_11_cout));  // open: cin
  FA fa_12 (.a(r7[3]), .b(r6[4]), .cin(r5[5]), .s(fa_12_s), .cout(fa_12_cout));
  FA fa_13 (.a(fa_16_cout), .b(fa_12_s), .cin(fa_11_s), .s(fa_13_s), .cout(fa_13_cout));
  FA fa_14 (.a(fa_13_cout), .b(fa_12_cout), .cin(fa_10_s), .s(fa_14_s), .cout(fa_14_cout));
  FA fa_15 (.a(fa_18_cout), .b(fa_14_s), .s(fa_56_s[11]), .cout(fa_56_s[12]));  // open: cin
  FA fa_16 (.a(r4[5]), .b(r3[6]), .cin(r2[7]), .s(fa_16_s), .cout(fa_16_cout));
  FA fa_17 (.a(r7[2]), .b(r6[3]), .cin(r5[4]), .s(fa_17_s), .cout(fa_17_cout));
  FA fa_18 (.a(fa_22_cout), .b(fa_17_cout), .cin(fa_13_s), .s(fa_18_s), .cout(fa_18_cout));
  FA fa_19 (.a(fa_24_cout), .b(fa_18_s), .s(fa_56_s[10]), .cout(undriven[11]));  // open: cin
  FA fa_20 (.a(r3[5]), .b(r2[6]), .cin(r1[7]), .s(fa_20_s), .cout(fa_20_cout));
  FA fa_21 (.a(r6[2]), .b(r5[3]), .cin(r4[4]), .s(fa_21_s), .cout(fa_21_cout));
  FA fa_22 (.a(fa_20_cout), .b(fa_17_s), .cin(fa_16_s), .s(fa_22_s), .cout(fa_22_cout));
  FA fa_23 (.a(fa_21_s), .b(fa_20_s), .s(fa_23_s), .cout(fa_23_cout));  // open: cin
  FA fa_24 (.a(fa_23_cout), .b(fa_21_cout), .cin(fa_22_s), .s(fa_24_s), .cout(fa_24_cout));
  FA fa_25 (.a(fa_29_cout), .b(fa_28_cout), .cin(fa_24_s), .s(fa_56_s[9]), .cout(undriven[10]));
  FA fa_26 (.a(r2[5]), .b(r1[6]), .cin(r0[7]), .s(fa_26_s), .cout(fa_26_cout));
  FA fa_27 (.a(r5[2]), .b(r4[3]), .cin(r3[4]), .s(fa_27_s), .cout(fa_27_cout));
  FA fa_28 (.a(fa_27_cout), .b(fa_26_cout), .cin(r7[1]), .s(fa_28_s), .cout(fa_28_cout));
  FA fa_29 (.a(fa_32_cout), .b(fa_28_s), .cin(fa_23_s), .s(fa_29_s), .cout(fa_29_cout));
  FA fa_30 (.a(fa_34_cout), .b(fa_33_cout), .cin(fa_29_s), .s(fa_56_s[8]), .cout(undriven[9]));
  FA fa_31 (.a(r2[4]), .b(r1[5]), .cin(r0[6]), .s(fa_31_s), .cout(fa_31_cout));
  FA fa_32 (.a(r6[1]), .b(fa_27_s), .cin(fa_26_s), .s(fa_32_s), .cout(fa_32_cout));
  FA fa_33 (.a(fa_36_cout), .b(fa_31_cout), .cin(r7[0]), .s(fa_33_s), .cout(fa_33_cout));
  FA fa_34 (.a(fa_38_cout), .b(fa_33_s), .cin(fa_32_s), .s(fa_34_s), .cout(fa_34_cout));
  FA fa_35 (.a(fa_40_cout), .b(fa_39_cout), .cin(fa_34_s), .s(fa_56_s[7]), .cout(undriven[8]));
  FA fa_36 (.a(r5[1]), .b(r4[2]), .cin(r3[3]), .s(fa_36_s), .cout(fa_36_cout));
  FA fa_37 (.a(r2[3]), .b(r1[4]), .cin(r0[5]), .s(fa_37_s), .cout(fa_37_cout));
  FA fa_38 (.a(fa_36_s), .b(fa_31_s), .s(fa_38_s), .cout(fa_38_cout));  // open: cin
  FA fa_39 (.a(fa_42_cout), .b(fa_37_cout), .cin(r6[0]), .s(fa_39_s), .cout(fa_39_cout));
  FA fa_40 (.a(fa_44_cout), .b(fa_39_s), .cin(fa_38_s), .s(fa_40_s), .cout(fa_40_cout));
  FA fa_41 (.a(fa_45_cout), .b(fa_40_s), .s(fa_56_s[6]), .cout(undriven[7]));  // open: cin
  FA fa_42 (.a(r5[0]), .b(r4[1]), .cin(r3[2]), .s(fa_42_s), .cout(fa_42_cout));
  FA fa_43 (.a(r1[3]), .b(r0[4]), .s(fa_43_s), .cout(fa_43_cout));  // open: cin
  FA fa_44 (.a(fa_43_cout), .b(fa_42_s), .cin(fa_37_s), .s(fa_44_s), .cout(fa_44_cout));
  FA fa_45 (.a(fa_48_cout), .b(fa_47_cout), .cin(fa_44_s), .s(fa_45_s), .cout(fa_45_cout));
  FA fa_46 (.a(fa_49_cout), .b(fa_45_s), .s(fa_56_s[5]), .cout(undriven[6]));  // open: cin
  FA fa_47 (.a(r4[0]), .b(r3[1]), .cin(r2[2]), .s(fa_47_s), .cout(fa_47_cout));
  FA fa_48 (.a(fa_51_cout), .b(fa_47_s), .cin(fa_43_s), .s(fa_48_s), .cout(fa_48_cout));
  FA fa_49 (.a(fa_52_cout), .b(fa_48_s), .s(fa_49_s), .cout(fa_49_cout));  // open: cin
  FA fa_50 (.a(fa_53_cout), .b(fa_49_s), .s(undriven[4]), .cout(undriven[5]));  // open: cin
  FA fa_51 (.a(r2[1]), .b(r1[2]), .cin(r0[3]), .s(fa_51_s), .cout(fa_51_cout));
  FA fa_52 (.a(fa_54_cout), .b(r3[0]), .cin(fa_51_s), .s(fa_52_s), .cout(fa_52_cout));
  FA fa_53 (.a(fa_55_cout), .b(fa_52_s), .s(fa_56_s[3]), .cout(fa_53_cout));  // open: cin
  FA fa_54 (.a(r2[0]), .b(r1[1]), .cin(r0[2]), .s(fa_54_s), .cout(fa_54_cout));
  FA fa_55 (.a(fa_56_cout), .b(fa_54_s), .s(fa_56_s[2]), .cout(fa_55_cout));  // open: cin
  FA fa_56 (.a(r1[0]), .b(r0[1]), .s(fa_56_s[1]), .cout(fa_56_cout));  // open: cin
  my16A_S my16a_s_1 (.a({fa_56_s, r0[0]}), .b(undriven), .s(AB));  // open: OP, overflow
endmodule

module uMull16 (
  input  [15:0] A,
  input  [15:0] B,
  output [15:0] AB,
  output Overflow
);

  wire and_1_out, my16a_s_1_overflow, my16a_s_2_overflow, or_1_out, or_2_out, or_3_out, or_4_out, or_5_out,
       or_6_out, or_7_out;
  wire [7:0] undriven, undriven_2;
  wire [15:0] my16a_s_1_s, umull8_1_ab, umull8_2_ab, umull8_3_ab;

  uMull8 umull8_1 (.A(A[7:0]), .B(B[7:0]), .AB(umull8_1_ab));
  uMull8 umull8_2 (.A(A[15:8]), .B(B[7:0]), .AB(umull8_2_ab));
  uMull8 umull8_3 (.A(A[7:0]), .B(B[15:8]), .AB(umull8_3_ab));
  or or_1 (or_1_out, A[8], A[9], A[10], A[11], A[12], A[13], A[14], A[15]);
  or or_2 (or_2_out, B[8], B[9], B[10], B[11], B[12], B[13], B[14], B[15]);
  and and_1 (and_1_out, or_1_out, or_2_out);
  or or_3 (or_3_out, umull8_2_ab[8], umull8_2_ab[9], umull8_2_ab[10], umull8_2_ab[11], umull8_2_ab[12], umull8_2_ab[13], umull8_2_ab[14], umull8_2_ab[15]);
  my16A_S my16a_s_1 (
    .a(umull8_1_ab), .b({umull8_2_ab[7:0], undriven}), .s(my16a_s_1_s), .overflow(my16a_s_1_overflow));  // open: OP
  or or_4 (or_4_out, my16a_s_1_overflow, or_3_out);
  my16A_S my16a_s_2 (
    .a(my16a_s_1_s), .b({umull8_3_ab[7:0], undriven_2}), .s(AB), .overflow(my16a_s_2_overflow));  // open: OP
  or or_5 (or_5_out, umull8_3_ab[8], umull8_3_ab[9], umull8_3_ab[10], umull8_3_ab[11], umull8_3_ab[12], umull8_3_ab[13], umull8_3_ab[14], umull8_3_ab[15]);
  or or_6 (or_6_out, or_4_out, or_5_out);
  or or_7 (or_7_out, my16a_s_2_overflow, or_6_out);
  or or_8 (Overflow, or_7_out, and_1_out);
endmodule

module SetSign (
  input  [15:0] A,
  input  S,
  output [15:0] U
);

  wire [14:0] negator_1_out;

  Negator #(.width(15)) negator_1 (.in(A[14:0]), .out(negator_1_out));
  Multiplexer #(.width(15)) multiplexer_1 (.in0(A[14:0]), .in1(negator_1_out), .out(U[14:0]), .sel(S));

  assign U[15] = S;
endmodule

module GetSign (
  input  [15:0] A,
  output [15:0] U,
  output S
);

  wire [14:0] negator_1_out;

  Negator #(.width(15)) negator_1 (.in(A[14:0]), .out(negator_1_out));
  Multiplexer #(.width(15)) multiplexer_1 (.in0(A[14:0]), .in1(negator_1_out), .out(U[14:0]), .sel(A[15]));

  assign S = A[15];
  assign U[15] = 1'b0;
endmodule
